# Fritzing sketch Device (saved by Fritzing 0.8.7b)
circuit board: 8.46667cm x 5.64444cm
breadboards: 1

parts:
  T1 = TMP36 Temperature Sensor [package="TO92 [THT]"]
  R3 = Resistor [tolerance=±5% resistance=220 package=THT]
  R1 = Resistor [tolerance=±5% resistance=220 package=THT]
  Part1 = Arduino Nano (Rev3.0)
  LED_Out = LED - 5mm [color="Red (633nm)" package="5 mm [THT]"]
  CDS = PHOTOCELL [package=photocell]
  Door = Pushbutton [package="[SMD]"]
  XBee_Adaptor = XBEE-1 [package=xbee-1]
  R4 = Resistor [tolerance=±5% resistance=220 package=THT]
  R5 = Resistor [tolerance=±5% resistance=220 package=THT]

nets:
  5V: T1.+Vs, Part1.5V, CDS.P$1, XBee_Adaptor.VDD
  N1: T1.Vout, Part1.A1
  GND: T1.GND, R1.Pin_0, Part1.GND, Door.Pin_3, Door.Pin_4, XBee_Adaptor.GND, R4.Pin_0, R5.Pin_0
  N2: R3.Pin_0, Part1.A2, R4.Pin_1
  N3: R3.Pin_1, Part1.VIN
  N4: R1.Pin_1, LED_Out.cathode
  N5: Part1.D2, XBee_Adaptor.DOUT
  N6: Part1.D3, XBee_Adaptor.DIN
  N7: Part1.D4, Door.Pin_1, Door.Pin_2
  N8: Part1.A0, CDS.P$2, R5.Pin_1
  N9: Part1.D13/SCK, LED_Out.anode
